// Logisim project classTwo(ULA, basics sum).circ as structural Verilog
module HalfSum (
  input  a,
  input  b,
  output Sum,
  output Carry_Out
);

  xor xor_1 (Sum, a, b);
  and and_1 (Carry_Out, a, b);
endmodule

module FullSum (
  input  a,
  input  b,
  input  CarryIn,
  output S,
  output CarryOut
);

  wire halfsum_1_carry_out, halfsum_1_sum, halfsum_2_carry_out;

  HalfSum halfsum_1 (.a(a), .b(b), .Sum(halfsum_1_sum), .Carry_Out(halfsum_1_carry_out));
  HalfSum halfsum_2 (.a(halfsum_1_sum), .b(CarryIn), .Sum(S), .Carry_Out(halfsum_2_carry_out));
  or or_1 (CarryOut, halfsum_2_carry_out, halfsum_1_carry_out);
endmodule

module Sum (
  input  [3:0] in_1,
  input  [3:0] in_2,
  input  CarryIn,
  output CarryOut,
  output [3:0] out_5
);

  wire fullsum_1_carryout, fullsum_2_carryout, fullsum_3_carryout;

  // Probe on in_1
  // Probe on in_2
  // Probe on out_5
  FullSum fullsum_1 (.a(CarryIn), .b(in_2[0]), .CarryIn(in_1[0]), .S(out_5[0]), .CarryOut(fullsum_1_carryout));
  FullSum fullsum_2 (
    .a(fullsum_1_carryout), .b(in_2[1]), .CarryIn(in_1[1]), .S(out_5[1]), .CarryOut(fullsum_2_carryout));
  FullSum fullsum_3 (
    .a(fullsum_2_carryout), .b(in_2[2]), .CarryIn(in_1[2]), .S(out_5[2]), .CarryOut(fullsum_3_carryout));
  FullSum fullsum_4 (.a(fullsum_3_carryout), .b(in_2[3]), .CarryIn(in_1[3]), .S(out_5[3]), .CarryOut(CarryOut));
endmodule

module ULA (
  input  [15:0] A,
  input  [15:0] R,
  input  [15:0] B,
  input  [3:0] Op,
  output out_5
);

  wire [15:0] OutAnd, OutDenied, OutDiv, OutMult, OutNOt, OutOr, OutSub, OutSum, Xor;

  Comparator #(.width(16)) comparator_1 (.a(A), .b(B), .gt(out_5));  // open: eq, lt
  assign OutAnd = A & B;  // AND_Gate and_1, 16 bits wide
  assign OutOr = A | B;  // OR_Gate or_1, 16 bits wide
  assign OutNOt = ~A;  // NOT_Gate not_1, 16 bits wide
  assign Xor = ~(A ^ B);  // XNOR_Gate xnor_1, 16 bits wide
  Adder #(.width(16)) adder_1 (.a(A), .b(B), .out(OutSum));  // open: cin, cout
  Subtractor #(.width(16)) subtractor_1 (.a(A), .b(B), .out(OutSub));  // open: bin, bout
  Multiplier #(.width(16)) multiplier_1 (.a(A), .b(B), .out(OutMult));  // open: cin, cout
  Divider #(.width(16)) divider_1 (.a(A), .b(B), .out(OutDiv));  // open: upper, rem
  Negator #(.width(16)) negator_1 (.in(A), .out(OutDenied));
  Multiplier #(.width(16)) multiplier_2 (.a(A), .b(B), .out(OutMult));  // open: cin, cout
  Multiplexer #(.select(4), .width(16)) multiplexer_1 (
    .in0(OutSum), .in1(OutMult), .in2(OutAnd), .in3(OutNOt), .in4(OutOr), .in5(OutDenied), .in6(OutDiv),
    .in7(OutSub), .in8(Xor), .out(R), .sel(Op));  // open: in9, in10, in11, in12, in13, in14, in15, en
endmodule
